# Fritzing sketch halloween-project (saved by Fritzing 0.9.3b)
circuit board: 8.46667cm x 5.64444cm
breadboards: 1

parts:
  Part1 = HC-SR501 Body Sensor Module
  Part2 = Adafruit PCA9685 PWM/Servo Breakout [part_number=815]
  YwRobot_Power_Supply1 = YwRobot Breadboard Power Supply [part_number=545043]  # not connected
  WeMos_D1_Mini1 = WeMos D1 Mini
  SP1 = SPEAKER [package=pcb_mount_speaker]
  DFRobot_DFPlayer_Mini1 = DFRobot DFPlayer Mini [part_number=DFR0299]
  J2 = Basic Servo  # not connected
  J3 = Basic Servo  # not connected
  J4 = Basic Servo  # not connected
  J5 = Basic Servo  # not connected
  J6 = Basic Servo  # not connected
  J7 = Basic Servo  # not connected
  J8 = Basic Servo  # not connected
  J9 = Basic Servo  # not connected
  J1 = Basic Servo

nets (from the breadboard view):
  VCC: Part1.VCC, Part2.PWRIN, Part2.VCC, WeMos_D1_Mini1.5V, DFRobot_DFPlayer_Mini1.VCC
  N1: Part1.OUT, WeMos_D1_Mini1.D7
  GND: Part1.GND, Part2.GND, WeMos_D1_Mini1.G, DFRobot_DFPlayer_Mini1.GND-1, DFRobot_DFPlayer_Mini1.GND-2, J1.gnd
  N2: Part2.PWM0, J1.pulse
  N3: Part2.5.0V, J1.vcc
  N4: Part2.SDA, WeMos_D1_Mini1.D2
  N5: Part2.SCL, WeMos_D1_Mini1.D1
  N6: WeMos_D1_Mini1.D5, DFRobot_DFPlayer_Mini1.TX
  N7: WeMos_D1_Mini1.D6, DFRobot_DFPlayer_Mini1.RX
  N8: SP1.+, DFRobot_DFPlayer_Mini1.SPK_2
  N9: SP1.-, DFRobot_DFPlayer_Mini1.SPK_1

notes:
  5V

custom parts:
  HC-SR501 Body Sensor Module: Pyroelectric Infrared PIR Motion Sensor Detector Module
  Adafruit PCA9685 PWM/Servo Breakout: Using only two pins, control 16 free-running PWM outputs! I2C-controlled PWM driver with a built in clock. Unlike the TLC5940 family, you do not need to continuously send it signal tying up your microcontroller, its completely free running! 5V compliant, which means you can control it from a 3.3V microcontroller and still safely drive up to 6V outputs (this is good for when you want to control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
  YwRobot Breadboard Power Supply: The YwRobot Breadboard Power Supply (MB-V2) has two power rails; they can be 5V or 3V3. Power to the module can be provided through the female USB socket or through the A10 (female) 2.1mm power jack.
